# Fritzing sketch Tea-dipper (saved by Fritzing 0.9.4)
breadboards: 2

parts:
  LCD1 = LCD screen  # not connected
  S1 = Pushbutton [package="[SMD]"]
  S2 = Pushbutton [package="[SMD]"]
  J1 = Piezo Speaker  # not connected
  R1 = Rotary Potentiometer (Small) [maximum_resistance=100kΩ package=THT]  # not connected
  Part1 = Arduino Uno (Rev3)  # not connected

nets:
  N1: S1.Pin_1, S1.Pin_2
  N2: S1.Pin_3, S1.Pin_4
  N3: S2.Pin_1, S2.Pin_2
  N4: S2.Pin_3, S2.Pin_4
